// Logisim project CPU.circ as structural Verilog: 5 circuits, main circuit main
module main (
  input  clear,
  input  enable,
  input  clock
);

  wire and_1_out, and_2_out, and_3_out, comparator_1_eq, comparator_1_gt, comparator_2_eq, comparator_3_eq,
       comparator_4_gt, comparator_5_lt, comparator_6_eq, decoder_1_out0, decoder_1_out1, not_1_out, undriven;
  wire [5:0] A_out;
  wire [14:0] bit_extender_3_out;
  wire [15:0] alu_1_out_4, bit_extender_1_out, bit_extender_2_out, bit_extender_4_out, Fetch_out_6,
       memory_1_out_6, memory_1_out_7, memory_1_out_8, memory_1_out_9, memory_1_out_10, memory_1_out_11,
       memory_1_out_12, memory_1_out_13, memory_1_out_14, memory_1_out_15, memory_1_out_16, memory_1_out_17,
       memory_1_out_18, memory_1_out_19, memory_1_out_20, memory_1_out_21, multiplexer_1_out,
       multiplexer_3_out, ram_1_data, register_file_1_read_1, register_file_1_read__2;

  Fetching Fetch (
    .clear(clear), .clock(clock), .in_3(bit_extender_1_out), .enable(enable), .branch(comparator_3_eq),
    .out_6(Fetch_out_6));
  assign bit_extender_1_out = {{8{1'b0}}, Fetch_out_6[7:0]};  // Bit_Extender bit_extender_1
  Comparator #(.width(4)) comparator_1 (
    .a(Fetch_out_6[15:12]), .b(4'b1011), .gt(comparator_1_gt), .eq(comparator_1_eq));  // open: lt
  Comparator #(.width(4)) comparator_2 (.a(Fetch_out_6[15:12]), .b(4'b1010), .eq(comparator_2_eq));  // open: gt, lt
  Comparator #(.width(4)) comparator_3 (.a(Fetch_out_6[15:12]), .b(4'b1100), .eq(comparator_3_eq));  // open: gt, lt
  Comparator #(.width(16)) comparator_4 (.a(bit_extender_4_out), .b(16'h7fff), .gt(comparator_4_gt));  // open: eq, lt
  Comparator #(.width(16)) comparator_5 (.a(bit_extender_4_out), .b(16'h8010), .lt(comparator_5_lt));  // open: gt, eq
  Multiplexer #(.width(16)) multiplexer_1 (
    .in0(register_file_1_read_1), .in1(bit_extender_1_out), .out(multiplexer_1_out), .sel(comparator_1_gt));  // open: en
  not not_1 (not_1_out, Fetch_out_6[4]);
  and and_1 (and_1_out, comparator_4_gt, comparator_5_lt);
  Multiplexer multiplexer_2 (.in0(undriven), .sel(comparator_2_eq));  // open: in1, out, en
  Register_File register_file_1 (
    .Write_Value(alu_1_out_4), .Clock(enable), .Write_Signal(comparator_2_eq),
    .Write_Address(Fetch_out_6[11:8]), .Clear_signal(clear), .Read_1(register_file_1_read_1),
    .Read_Address_1(Fetch_out_6[7:4]), .Read__2(register_file_1_read__2), .Read_Address_2(Fetch_out_6[3:0]));
  and and_2 (and_2_out, comparator_1_eq, not_1_out);
  and and_3 (and_3_out, comparator_1_eq, and_1_out);
  ALU alu_1 (
    .int1(register_file_1_read__2), .int2(multiplexer_1_out), .opcode(Fetch_out_6[15:12]), .out_4(alu_1_out_4));
  assign bit_extender_2_out = {{12{1'b0}}, Fetch_out_6[7:4]};  // Bit_Extender bit_extender_2
  assign bit_extender_3_out = {{11{1'b0}}, Fetch_out_6[3:0]};  // Bit_Extender bit_extender_3
  Memory memory_1 (
    .write_data(multiplexer_3_out), .Clock(clock), .Write_address(Fetch_out_6[3:0]), .enable(and_3_out),
    .out_6(memory_1_out_6), .Clear(clear), .out_7(memory_1_out_7), .out_8(memory_1_out_8),
    .out_9(memory_1_out_9), .out_10(memory_1_out_10), .out_11(memory_1_out_11), .out_12(memory_1_out_12),
    .out_13(memory_1_out_13), .out_14(memory_1_out_14), .out_15(memory_1_out_15), .out_16(memory_1_out_16),
    .out_17(memory_1_out_17), .out_18(memory_1_out_18), .out_19(memory_1_out_19), .out_20(memory_1_out_20),
    .out_21(memory_1_out_21));
  DotMatrix #(.inputtype("row"), .matrixcols(16), .matrixrows(16)) dotmatrix_1 (
    .row0(memory_1_out_6), .row1(memory_1_out_7), .row2(memory_1_out_8), .row3(memory_1_out_9),
    .row4(memory_1_out_10), .row5(memory_1_out_11), .row6(memory_1_out_12), .row7(memory_1_out_13),
    .row8(memory_1_out_14), .row9(memory_1_out_15), .row10(memory_1_out_16), .row11(memory_1_out_17),
    .row12(memory_1_out_18), .row13(memory_1_out_19), .row14(memory_1_out_20), .row15(memory_1_out_21));
  assign bit_extender_4_out = {{12{1'b0}}, Fetch_out_6[3:0]};  // Bit_Extender bit_extender_4
  RAM #(.addrWidth(15), .dataWidth(16), .bus("separate")) ram_1 (
    .addr(bit_extender_3_out), .din(bit_extender_2_out), .data(ram_1_data), .str(and_2_out), .clk(clock),
    .ld(decoder_1_out1), .clr(clear));  // open: sel
  Decoder decoder_1 (.out0(decoder_1_out0), .out1(decoder_1_out1), .sel(comparator_2_eq));  // open: en
  Comparator #(.width(16)) comparator_6 (.a(bit_extender_4_out), .b(16'h8010), .eq(comparator_6_eq));  // open: gt, lt
  Multiplexer #(.width(16)) multiplexer_3 (
    .in0(ram_1_data), .in1({{10{1'b0}}, A_out}), .out(multiplexer_3_out), .sel(comparator_6_eq));  // open: en
  Button button (.out(A_out[2]));
  Button v (.out(A_out[5]));
  Button button_2 (.out(A_out[4]));
  Button button_3 (.out(A_out[3]));
  Button A (.out(A_out[0]));
  Button B (.out(A_out[1]));
endmodule

module ALU (
  input  [15:0] int1,
  input  [15:0] int2,
  input  [3:0] opcode,
  output [15:0] out_4
);

  wire comparator_1_eq, comparator_2_lt, comparator_3_eq, not_1_out;
  wire [3:0] bitselector_1_out;
  wire [15:0] adder_1_out, and_1_out, bit_extender_1_out, bit_extender_2_out, bit_extender_3_out,
       multiplier_1_out, not_2_out, or_1_out, shifter_1_out, shifter_2_out, subtractor_1_out, xor_1_out;

  BitSelector #(.width(16), .group(4)) bitselector_1 (.in(int2), .out(bitselector_1_out), .sel(2'b00));
  Comparator #(.width(16)) comparator_1 (.a(int1), .b({16{1'b0}}), .eq(comparator_1_eq));  // open: gt, lt
  Adder #(.width(16)) adder_1 (.a(int1), .b(int2), .out(adder_1_out));  // open: cin, cout
  Subtractor #(.width(16)) subtractor_1 (.a(int1), .b(int2), .out(subtractor_1_out));  // open: bin, bout
  Multiplier #(.width(16)) multiplier_1 (.a(int1), .b(int2), .out(multiplier_1_out));  // open: cin, cout
  Shifter #(.width(16)) shifter_1 (.in(int1), .\dist (bitselector_1_out), .out(shifter_1_out));
  Shifter #(.width(16), .shift("lr")) shifter_2 (.in(int1), .\dist (bitselector_1_out), .out(shifter_2_out));
  assign bit_extender_1_out = {{15{1'b0}}, comparator_2_lt};  // Bit_Extender bit_extender_1
  Comparator #(.width(16)) comparator_2 (.a(int1), .b(int2), .lt(comparator_2_lt));  // open: gt, eq
  Comparator #(.width(16)) comparator_3 (.a(int1), .b({16{1'b0}}), .eq(comparator_3_eq));  // open: gt, lt
  not not_1 (not_1_out, comparator_3_eq);
  assign bit_extender_2_out = {{15{1'b0}}, comparator_1_eq};  // Bit_Extender bit_extender_2
  assign bit_extender_3_out = {{15{1'b0}}, not_1_out};  // Bit_Extender bit_extender_3
  assign and_1_out = int1 & int2;  // AND_Gate and_1, 16 bits wide
  assign or_1_out = int1 | int2;  // OR_Gate or_1, 16 bits wide
  assign xor_1_out = int2 ^ int1;  // XOR_Gate xor_1, 16 bits wide
  assign not_2_out = ~int1;  // NOT_Gate not_2, 16 bits wide
  Multiplexer #(.select(4), .width(16)) multiplexer_1 (
    .in0(and_1_out), .in1(or_1_out), .in2(xor_1_out), .in3(not_2_out), .in4(adder_1_out),
    .in5(subtractor_1_out), .in6(multiplier_1_out), .in7(bit_extender_1_out), .in8(shifter_1_out),
    .in9(shifter_2_out), .in10(int1), .in11(int1), .in12(int2), .in13(16'h1), .in14(bit_extender_2_out),
    .in15(bit_extender_3_out), .out(out_4), .sel(opcode));  // open: en
endmodule

module Register_File (
  input  [15:0] Write_Value,
  input  Clock,
  input  [3:0] Read_Address_1,
  input  Write_Signal,
  input  [3:0] Write_Address,
  input  [3:0] Read_Address_2,
  input  Clear_signal,
  output [15:0] Read_1,
  output [15:0] Read__2
);

  wire decoder_1_out0, decoder_1_out1, decoder_1_out2, decoder_1_out3, decoder_1_out4, decoder_1_out5,
       decoder_1_out6, decoder_1_out7, decoder_1_out8, decoder_1_out9, decoder_1_out10, decoder_1_out11,
       decoder_1_out12, decoder_1_out13, decoder_1_out14, decoder_1_out15;
  wire [15:0] register_1_q, register_2_q, register_3_q, register_4_q, register_5_q, register_6_q,
       register_7_q, register_8_q, register_9_q, register_10_q, register_11_q, register_12_q, register_13_q,
       register_14_q, register_15_q, register_16_q;

  Decoder #(.select(4), .disabled(0)) decoder_1 (
    .out0(decoder_1_out0), .out1(decoder_1_out1), .out2(decoder_1_out2), .out3(decoder_1_out3),
    .out4(decoder_1_out4), .out5(decoder_1_out5), .out6(decoder_1_out6), .out7(decoder_1_out7),
    .out8(decoder_1_out8), .out9(decoder_1_out9), .out10(decoder_1_out10), .out11(decoder_1_out11),
    .out12(decoder_1_out12), .out13(decoder_1_out13), .out14(decoder_1_out14), .out15(decoder_1_out15),
    .sel(Write_Address), .en(Write_Signal));
  Register #(.width(16)) register_1 (
    .D(Write_Value), .en(decoder_1_out0), .Q(register_1_q), .clk(Clock), .clr(Clear_signal));
  Register #(.width(16)) register_2 (
    .D(Write_Value), .en(decoder_1_out2), .Q(register_2_q), .clk(Clock), .clr(Clear_signal));
  Register #(.width(16)) register_3 (
    .D(Write_Value), .en(decoder_1_out4), .Q(register_3_q), .clk(Clock), .clr(Clear_signal));
  Register #(.width(16)) register_4 (
    .D(Write_Value), .en(decoder_1_out6), .Q(register_4_q), .clk(Clock), .clr(Clear_signal));
  Register #(.width(16)) register_5 (
    .D(Write_Value), .en(decoder_1_out8), .Q(register_5_q), .clk(Clock), .clr(Clear_signal));
  Register #(.width(16)) register_6 (
    .D(Write_Value), .en(decoder_1_out10), .Q(register_6_q), .clk(Clock), .clr(Clear_signal));
  Register #(.width(16)) register_7 (
    .D(Write_Value), .en(decoder_1_out12), .Q(register_7_q), .clk(Clock), .clr(Clear_signal));
  Register #(.width(16)) register_8 (
    .D(Write_Value), .en(decoder_1_out14), .Q(register_8_q), .clk(Clock), .clr(Clear_signal));
  Register #(.width(16)) register_9 (
    .D(Write_Value), .en(decoder_1_out1), .Q(register_9_q), .clk(Clock), .clr(Clear_signal));
  Register #(.width(16)) register_10 (
    .D(Write_Value), .en(decoder_1_out3), .Q(register_10_q), .clk(Clock), .clr(Clear_signal));
  Register #(.width(16)) register_11 (
    .D(Write_Value), .en(decoder_1_out5), .Q(register_11_q), .clk(Clock), .clr(Clock));
  Register #(.width(16)) register_12 (
    .D(Write_Value), .en(decoder_1_out7), .Q(register_12_q), .clk(Clock), .clr(Clear_signal));
  Register #(.width(16)) register_13 (
    .D(Write_Value), .en(decoder_1_out9), .Q(register_13_q), .clk(Clock), .clr(Clear_signal));
  Register #(.width(16)) register_14 (
    .D(Write_Value), .en(decoder_1_out11), .Q(register_14_q), .clk(Clock), .clr(Clear_signal));
  Register #(.width(16)) register_15 (
    .D(Write_Value), .en(decoder_1_out13), .Q(register_15_q), .clk(Clock), .clr(Clear_signal));
  Register #(.width(16)) register_16 (
    .D(Write_Value), .en(decoder_1_out15), .Q(register_16_q), .clk(Clock), .clr(Clear_signal));
  Multiplexer #(.select(4), .width(16)) multiplexer_1 (
    .in0(register_1_q), .in1(register_9_q), .in2(register_2_q), .in3(register_10_q), .in4(register_3_q),
    .in5(register_11_q), .in6(register_4_q), .in7(register_12_q), .in8(register_5_q), .in9(register_13_q),
    .in10(register_6_q), .in11(register_14_q), .in12(register_7_q), .in13(register_15_q),
    .in14(register_8_q), .in15(register_16_q), .out(Read_1), .sel(Read_Address_1));  // open: en
  Multiplexer #(.select(4), .width(16)) multiplexer_2 (
    .in0(register_1_q), .in1(register_9_q), .in2(register_2_q), .in3(register_10_q), .in4(register_3_q),
    .in5(register_11_q), .in6(register_4_q), .in7(register_12_q), .in8(register_5_q), .in9(register_13_q),
    .in10(register_6_q), .in11(register_14_q), .in12(register_7_q), .in13(register_15_q),
    .in14(register_8_q), .in15(register_16_q), .out(Read__2), .sel(Read_Address_2));  // open: en
endmodule

module Memory (
  input  [15:0] write_data,
  input  Clear,
  input  Clock,
  input  [3:0] Write_address,
  input  enable,
  output [15:0] out_6,
  output [15:0] out_7,
  output [15:0] out_8,
  output [15:0] out_9,
  output [15:0] out_10,
  output [15:0] out_11,
  output [15:0] out_12,
  output [15:0] out_13,
  output [15:0] out_14,
  output [15:0] out_15,
  output [15:0] out_16,
  output [15:0] out_17,
  output [15:0] out_18,
  output [15:0] out_19,
  output [15:0] out_20,
  output [15:0] out_21
);

  wire decoder_1_out0, decoder_1_out1, decoder_1_out2, decoder_1_out3, decoder_1_out4, decoder_1_out5,
       decoder_1_out6, decoder_1_out7, decoder_1_out8, decoder_1_out9, decoder_1_out10, decoder_1_out11,
       decoder_1_out12, decoder_1_out13, decoder_1_out14, decoder_1_out15;

  Decoder #(.select(4), .disabled(0)) decoder_1 (
    .out0(decoder_1_out0), .out1(decoder_1_out1), .out2(decoder_1_out2), .out3(decoder_1_out3),
    .out4(decoder_1_out4), .out5(decoder_1_out5), .out6(decoder_1_out6), .out7(decoder_1_out7),
    .out8(decoder_1_out8), .out9(decoder_1_out9), .out10(decoder_1_out10), .out11(decoder_1_out11),
    .out12(decoder_1_out12), .out13(decoder_1_out13), .out14(decoder_1_out14), .out15(decoder_1_out15),
    .sel(Write_address), .en(enable));
  Register #(.width(16)) register_1 (.D(write_data), .en(decoder_1_out0), .Q(out_6), .clk(Clock), .clr(Clear));
  Register #(.width(16)) register_2 (.D(write_data), .en(decoder_1_out2), .Q(out_8), .clk(Clock), .clr(Clear));
  Register #(.width(16)) register_3 (.D(write_data), .en(decoder_1_out4), .Q(out_10), .clk(Clock), .clr(Clear));
  Register #(.width(16)) register_4 (.D(write_data), .en(decoder_1_out6), .Q(out_12), .clk(Clock), .clr(Clear));
  Register #(.width(16)) register_5 (.D(write_data), .en(decoder_1_out8), .Q(out_14), .clk(Clock), .clr(Clear));
  Register #(.width(16)) register_6 (.D(write_data), .en(decoder_1_out10), .Q(out_16), .clk(Clock), .clr(Clear));
  Register #(.width(16)) register_7 (.D(write_data), .en(decoder_1_out12), .Q(out_18), .clk(Clock), .clr(Clear));
  Register #(.width(16)) register_8 (.D(write_data), .en(decoder_1_out14), .Q(out_20), .clk(Clock), .clr(Clear));
  Register #(.width(16)) register_9 (.D(write_data), .en(decoder_1_out1), .Q(out_7), .clk(Clock), .clr(Clear));
  Register #(.width(16)) register_10 (.D(write_data), .en(decoder_1_out3), .Q(out_9), .clk(Clock), .clr(Clear));
  Register #(.width(16)) register_11 (.D(write_data), .en(decoder_1_out5), .Q(out_11), .clk(Clock), .clr(Clear));
  Register #(.width(16)) register_12 (.D(write_data), .en(decoder_1_out7), .Q(out_13), .clk(Clock), .clr(Clear));
  Register #(.width(16)) register_13 (.D(write_data), .en(decoder_1_out9), .Q(out_15), .clk(Clock), .clr(Clear));
  Register #(.width(16)) register_14 (.D(write_data), .en(decoder_1_out11), .Q(out_17), .clk(Clock), .clr(Clear));
  Register #(.width(16)) register_15 (.D(write_data), .en(decoder_1_out13), .Q(out_19), .clk(Clock), .clr(Clear));
  Register #(.width(16)) register_16 (.D(write_data), .en(decoder_1_out15), .Q(out_21), .clk(Clock), .clr(Clear));
endmodule

module Fetching (
  input  clear,
  input  clock,
  input  [15:0] in_3,
  input  enable,
  input  branch,
  output [15:0] out_6
);

  wire [15:0] adder_1_out, multiplexer_1_out, register_1_q;

  Register #(.width(16)) register_1 (.D(adder_1_out), .en(enable), .Q(register_1_q), .clk(clock), .clr(clear));
  Adder #(.width(16)) adder_1 (.a(register_1_q), .b(multiplexer_1_out), .out(adder_1_out));  // open: cin, cout
  Multiplexer #(.width(16)) multiplexer_1 (.in0(16'h1), .in1(in_3), .out(multiplexer_1_out), .sel(branch));  // open: en
  ROM #(.addrWidth(16), .dataWidth(16)) rom_1 (.addr(register_1_q), .data(out_6));  // open: sel
endmodule
